# Fritzing sketch LTG-Schematic (saved by Fritzing 0.8.7b)
breadboards: 1

parts:
  IR_Sensor_Array = 5-ir-array-sensor [package=THT]
  Part1 = Adafruit PowerBoost 1000C [part_number="Adafruit #2465"]
  Steering_Motor = DC Motor
  Stock_USB = USB Connectors [package=usb-a-h]
  AutoPhat_MotorDriver/IMU = SparkFun_Auto_pHAT
  After_market_battery = LIPO-2000mAh [package=lipo-2000]
  Drive_Motor = DC Motor
  Stock_Switch = SPDT Slide Switch [package=ayz0202]
  Stock_Battery = LIPO-1000mAh [package=lipo-1000]
  Part2 = LilyPad Slide Switch

nets:
  N1: IR_Sensor_Array.S5, AutoPhat_MotorDriver/IMU.GPIO26
  N2: IR_Sensor_Array.S4, AutoPhat_MotorDriver/IMU.GPIO19
  N3: IR_Sensor_Array.S3, AutoPhat_MotorDriver/IMU.GPIO13
  N4: IR_Sensor_Array.S2, AutoPhat_MotorDriver/IMU.GPIO6
  GND: IR_Sensor_Array.S1, IR_Sensor_Array.GND, Part1.GND, Stock_USB.GND, AutoPhat_MotorDriver/IMU.GND-6, AutoPhat_MotorDriver/IMU.GPIO5, AutoPhat_MotorDriver/IMU.GND-30, AutoPhat_MotorDriver/IMU.GND-39, After_market_battery.-, Stock_Battery.-
  N5: IR_Sensor_Array.VCC, AutoPhat_MotorDriver/IMU.GPIO9
  N6: Part1.VBUS, Stock_USB.D+, Stock_Switch.3, Stock_Battery.+
  N7: Part1.VLIPO, Part2.ON
  N8: Part1.5.0V, AutoPhat_MotorDriver/IMU.MTR-PWR, AutoPhat_MotorDriver/IMU.5V-IN, AutoPhat_MotorDriver/IMU.5V-2, AutoPhat_MotorDriver/IMU.5V-4
  N9: Steering_Motor.pin_1, AutoPhat_MotorDriver/IMU.AOUT2
  N10: Steering_Motor.pin_2, AutoPhat_MotorDriver/IMU.AOUT1
  N11: AutoPhat_MotorDriver/IMU.BOUT1, Drive_Motor.pin_2
  N12: AutoPhat_MotorDriver/IMU.BOUT2, Drive_Motor.pin_1
  N13: After_market_battery.+, Part2.OFF

custom parts:
  5-ir-array-sensor: 5 IR array sensor.
  Adafruit PowerBoost 1000C: PowerBoost 1000C is the perfect power supply for your portable project! With a built-in load-sharing battery charger circuit, you'll be able to keep your power-hungry project running even while recharging the battery! This little DC/DC boost converter module can be powered by any 3.7V LiIon/LiPoly battery, and convert the battery output to 5.2V DC for running your 5V projects.
  SparkFun_Auto_pHAT: Sparkfun SparkFun_Auto_pHAT Raspberry PI hat.
